# Fritzing sketch Schematic (saved by Fritzing 0.9.3b)
breadboards: 1

parts:
  S1 = Momentary Switch [package=ksa_sealed_tac_switch]
  R1 = Resistor [tolerance=±5% resistance=220 package=THT]
  LED1 = LED - 5mm [color="Red (633nm)" package="5 mm [THT]"]
  R2 = Resistor [tolerance=±5% resistance=220 package=THT]
  Part1 = Arduino Uno (Rev3)
  Q1 = NPN-Transistor [package="TO92 [THT]"]
  Q2 = NPN-Transistor [package="TO92 [THT]"]

nets:
  N1: S1.2, Part1.5V
  N2: S1.3, R1.Pin_1, Part1.D2
  N3: R1.Pin_0, LED1.anode, Part1.GND, Q1.E, Q2.C
  N4: LED1.cathode, R2.Pin_1
  N5: R2.Pin_0, Part1.D13/SCK
  N6: Part1.D6_PWM, Q1.B
  N7: Part1.D7, Q2.B
